// Logisim project main.circ as structural Verilog: 12 circuits, main circuit main
module main (
  output out_1,
  output [1:0] ATACK_MODE
);

  wire adder_10_out, and_1_out, and_7_out, and_8_out, and_9_out, and_10_out, and_11_out, and_12_out,
       and_13_out, and_14_out, and_15_out, and_16_out, and_17_out, and_18_out, and_19_out, and_20_out,
       and_21_out, and_22_out, and_23_out, and_24_out, and_25_out, and_26_out, and_27_out, and_28_out,
       and_29_out, and_30_out, and_31_out, and_32_out, and_33_out, and_34_out, ATCinisW, ATCinit,
       ATCInpFlpre, ATCnEhp, ATCnewENclc, ATCpWIN, buffer_1_out, buffer_2_out, button_1_out, button_2_out,
       changePCx, changePCy, chGM, CHHPinmove, comparator_1_eq, comparator_2_eq, comparator_3_eq,
       comparator_4_eq, comparator_5_eq, comparator_6_lt, comparator_7_gt, comparator_8_lt, comparator_9_gt,
       comparator_10_eq, comparator_11_eq, comparator_12_eq, comparator_13_eq, comparator_14_eq,
       comparator_15_eq, comparator_16_eq, comparator_17_eq, comparator_18_eq, comparator_19_lt,
       comparator_20_lt, comparator_21_gt, comparator_22_lt, comparator_23_gt, comparator_24_lt,
       comparator_25_gt, comparator_26_lt, comparator_27_gt, comparator_28_lt, comparator_29_gt,
       comparator_30_eq, comparator_31_eq, comparator_32_eq, comparator_33_eq, comparator_35_eq,
       comparator_36_eq, comparator_38_eq, comparator_42_eq, comparator_42_gt, comparator_42_lt,
       comparator_43_eq, comparator_44_eq, comparator_45_eq, comparator_46_eq, comparator_47_eq,
       comparator_48_eq, comparator_49_eq, comparator_50_eq, comparator_51_eq, comparator_52_eq,
       comparator_53_eq, comparator_54_eq, comparator_55_eq, comparator_56_eq, comparator_57_eq,
       comparator_58_lt, comparator_59_gt, comparator_60_lt, comparator_61_gt, comparator_62_lt,
       comparator_63_gt, comparator_64_lt, comparator_65_gt, comparator_66_lt, comparator_67_gt,
       comparator_68_eq, comparator_69_eq, comparator_70_eq, comparator_71_eq, comparator_72_eq,
       comparator_72_lt, comparator_73_gt, comparator_74_gt, comparator_75_gt, comparator_76_gt,
       comparator_77_lt, comparator_78_lt, comparator_79_lt, comparator_80_lt, comparator_81_eq,
       comparator_82_eq, CONSOLE_PRINTER_it_worked, demultiplexer_1_out1, gS0, gS1, gS2, InpFl1, InpFlmove1,
       InpFlmove2, InpFlmove31, InpFlmove32, InpFlmove33, InpFlmove34, InpFlmove35, InpFlpre, InpFlpreAtc,
       InpFlpreSTRT, \InpFlpreС , INV1ch, INV2ch, INV3ch, INV4ch, INV5ch, invchn, ITEMinCELL, itemRES1,
       itemRES2, itemRES3, itemRES4, itemRES5, letsPrint, LoadMap, mainClk, mainRES, MapLevelCh, mapPREst,
       mapPREst1, memReadyToPrint, not_1_out, not_2_out, not_3_out, not_4_out, not_5_out, not_6_out,
       not_7_out, not_8_out, not_9_out, not_10_out, not_11_out, not_13_out, or_2_out, or_4_out, or_6_out,
       or_7_out, or_8_out, or_9_out, or_10_out, or_11_out, or_15_out, or_16_out, or_19_out, or_20_out,
       or_21_out, PLAYERHPCH, PlDirCh, printing_map_1_cond_of_change, pull_resistor_1_node,
       pull_resistor_4_node, qres, quick_18_out, quick_19_out, quick_21_out, register_26_q, StateCh,
       stMapCLC, stMapCLC1, stMapCLC2, TOPRINTRES, WonInp;
  wire [1:0] adder_5_out, ATCcurEN, ATCnewEN, bit_extender_3_out, bit_extender_4_out, bit_extender_5_out,
       bit_extender_6_out, gSto, NewPlDir, PlDir, subtractor_4_out;
  wire [2:0] adder_1_out, bit_extender_1_out, bit_extender_2_out, register_1_q;
  wire [3:0] adder_6_out, register_16_q;
  wire [7:0] adder_2_out, adder_3_out, adder_4_out, adder_7_out, adder_8_out, ATCInpKey, ENDMG, ENDMGst,
       enemies_1_hp, ENHP, ENHPst, ENimgChrst, ENIMN, ENNmChrst, food_1_givehp, graphic_elems_1_data,
       gStdtScrMem, InpKey, InpKeyall, INVENTORY1, INVENTORY1p, INVENTORY2, INVENTORY2p, INVENTORY3,
       INVENTORY3p, INVENTORY4, INVENTORY4p, INVENTORY5, INVENTORY5p, mapLevelCur, maps_1_xpp, maps_1_ypp,
       mapSTDATAreaded, memChar, multiplexer_1_out, multiplexer_2_out, multiplexer_3_out, multiplexer_4_out,
       multiplexer_8_out, multiplexer_9_out, NewMapLevelCh, NewPlayerHP, NewPLxOM, NewPLyOM, objectONmap,
       p_x_1_y, p_x_1_y_t, p_x_y, p_x_y_1, p_x_y_1_t, playerHPCUR, PLxOM, PLyOM,
       printing_map_1_char_on_screen, subtractor_1_out, subtractor_2_out, subtractor_3_out, subtractor_5_out,
       subtractor_6_out, subtractor_7_out, subtractor_8_out, subtractor_9_out, subtractor_10_out,
       subtractor_11_out, subtractor_12_out, weapon_1_dmg;
  wire [11:0] adder_9_out, MAP_tospace_ELEM, MapH, maps_1_height, maps_1_width, mapSTelemREAD, MapW, memN,
       multiplexer_10_out, p_x_1_y__elemOnMap, p_x_1_y__elemOnMap_t, p_x_y_1__elemOnMap,
       p_x_y_1__elemOnMap_t, p_x_y__elemOnMap, tpLen;

  or or_1 (letsPrint, memReadyToPrint, gS0);
  Comparator comparator_1 (.a(InpKey), .b(8'h31), .eq(comparator_1_eq));  // open: gt, lt
  Comparator comparator_2 (.a(InpKey), .b(8'h32), .eq(comparator_2_eq));  // open: gt, lt
  Comparator comparator_3 (.a(InpKey), .b(8'h33), .eq(comparator_3_eq));  // open: gt, lt
  Comparator comparator_4 (.a(InpKey), .b(8'h34), .eq(comparator_4_eq));  // open: gt, lt
  Comparator comparator_5 (.a(InpKey), .b(8'h35), .eq(comparator_5_eq));  // open: gt, lt
  Comparator comparator_6 (.a(p_x_y), .b(8'h65), .lt(comparator_6_lt));  // open: gt, eq
  Comparator comparator_7 (.a(p_x_y), .b(8'h60), .gt(comparator_7_gt));  // open: eq, lt
  Comparator comparator_8 (.a(p_x_y), .b(8'h6b), .lt(comparator_8_lt));  // open: gt, eq
  Comparator comparator_9 (.a(p_x_y), .b(8'h65), .gt(comparator_9_gt));  // open: eq, lt
  Comparator comparator_10 (.a(InpKeyall), .b(8'h31), .eq(comparator_10_eq));  // open: gt, lt
  Comparator comparator_11 (.a(InpKeyall), .b(8'h32), .eq(comparator_11_eq));  // open: gt, lt
  Comparator comparator_12 (.a(InpKeyall), .b(8'h33), .eq(comparator_12_eq));  // open: gt, lt
  Comparator comparator_13 (.a(InpKeyall), .b(8'h34), .eq(comparator_13_eq));  // open: gt, lt
  Comparator comparator_14 (.a(InpKeyall), .b(8'h35), .eq(comparator_14_eq));  // open: gt, lt
  quick quick_1 (.IN(demultiplexer_1_out1), .OUT(\InpFlpreС ));
  Demultiplexer #(.select(2), .disabled(0), .enable("false")) demultiplexer_1 (
    .out0(InpFlpreSTRT), .out1(demultiplexer_1_out1), .out2(ATCInpFlpre), .in(CONSOLE_PRINTER_it_worked),
    .sel(ATACK_MODE));  // open: out3
  consoler CONSOLE_PRINTER (
    .CLK(mainClk), .RESET(letsPrint), .IT_WORKED(CONSOLE_PRINTER_it_worked), .INPUT_CHAR(InpKeyall),
    .PRINT_SIZE(tpLen), .MEM_A(memN), .MEM_D(memChar));
  Multiplexer #(.width(8), .enable("false")) multiplexer_1 (
    .in0(NewPLxOM), .in1(maps_1_xpp), .out(multiplexer_1_out), .sel(gS0));
  or or_2 (or_2_out, changePCx, LoadMap);
  Register #(.width(12)) u_mapW (.D(maps_1_width), .Q(MapW), .clk(LoadMap));  // open: en, clr
  Register #(.width(3)) register_1 (.D(adder_1_out), .Q(register_1_q), .clk(and_1_out), .clr(TOPRINTRES));  // open: en
  and and_1 (and_1_out, comparator_19_lt, mainClk);
  quick quick_2 (.IN(InpFlpre), .OUT(TOPRINTRES));
  Comparator #(.width(2)) comparator_15 (.a(PlDir), .b(2'b00), .eq(comparator_15_eq));  // open: gt, lt
  Comparator #(.width(2)) comparator_16 (.a(PlDir), .b(2'b10), .eq(comparator_16_eq));  // open: gt, lt
  Comparator #(.width(2)) comparator_17 (.a(PlDir), .b(2'b01), .eq(comparator_17_eq));  // open: gt, lt
  Comparator #(.width(2)) comparator_18 (.a(PlDir), .b(2'b11), .eq(comparator_18_eq));  // open: gt, lt
  quick quick_3 (.IN(InpFlmove31), .OUT(INV1ch));
  and and_2 (InpFlmove31, comparator_1_eq, InpFlpre, ITEMinCELL);
  quick quick_4 (.IN(InpFlmove32), .OUT(INV2ch));
  and and_3 (InpFlmove32, comparator_2_eq, InpFlpre, ITEMinCELL);
  quick quick_5 (.IN(InpFlmove33), .OUT(INV3ch));
  and and_4 (InpFlmove33, comparator_3_eq, InpFlpre, ITEMinCELL);
  quick quick_6 (.IN(InpFlmove34), .OUT(INV4ch));
  and and_5 (InpFlmove34, comparator_4_eq, InpFlpre, ITEMinCELL);
  and and_6 (InpFlmove35, comparator_5_eq, InpFlpre, ITEMinCELL);
  quick quick_7 (.IN(InpFlmove35), .OUT(INV5ch));
  and and_7 (and_7_out, comparator_6_lt, comparator_7_gt);
  or or_3 (ITEMinCELL, and_7_out, and_8_out);
  and and_8 (and_8_out, comparator_8_lt, comparator_9_gt);
  Subtractor subtractor_1 (.a(InpKeyall), .b(8'h31), .out(subtractor_1_out));  // open: bin, bout
  Bit_Extender #(.out_width(3)) bit_extender_1 (.in(subtractor_1_out), .out(bit_extender_1_out));
  Demultiplexer #(.select(2), .width(8), .disabled(0), .enable("false")) demultiplexer_2 (
    .out1(InpKey), .out2(ATCInpKey), .in(InpKeyall), .sel(ATACK_MODE));  // open: out0, out3
  Register Xpp (.D(multiplexer_1_out), .Q(PLxOM), .clk(or_2_out));  // open: en, clr
  Adder #(.width(3)) adder_1 (.a(3'b001), .b(register_1_q), .out(adder_1_out));  // open: cin, cout
  Comparator #(.width(3)) comparator_19 (.a(3'b111), .b(register_1_q), .gt(InpFl1), .lt(comparator_19_lt));  // open: eq
  Comparator comparator_20 (.a(INVENTORY1p), .b(8'h65), .lt(comparator_20_lt));  // open: gt, eq
  and and_9 (and_9_out, comparator_20_lt, comparator_10_eq, comparator_21_gt);
  Comparator comparator_21 (.a(INVENTORY1p), .b(8'h60), .gt(comparator_21_gt));  // open: eq, lt
  Comparator comparator_22 (.a(INVENTORY2p), .b(8'h65), .lt(comparator_22_lt));  // open: gt, eq
  and and_10 (and_10_out, comparator_22_lt, comparator_11_eq, comparator_23_gt);
  Comparator comparator_23 (.a(INVENTORY2p), .b(8'h60), .gt(comparator_23_gt));  // open: eq, lt
  Comparator comparator_24 (.a(INVENTORY3p), .b(8'h65), .lt(comparator_24_lt));  // open: gt, eq
  and and_11 (and_11_out, comparator_24_lt, comparator_12_eq, comparator_25_gt);
  Comparator comparator_25 (.a(INVENTORY3p), .b(8'h60), .gt(comparator_25_gt));  // open: eq, lt
  Comparator comparator_26 (.a(INVENTORY4p), .b(8'h65), .lt(comparator_26_lt));  // open: gt, eq
  and and_12 (and_12_out, comparator_26_lt, comparator_13_eq, comparator_27_gt);
  Comparator comparator_27 (.a(INVENTORY4p), .b(8'h60), .gt(comparator_27_gt));  // open: eq, lt
  Comparator comparator_28 (.a(INVENTORY5p), .b(8'h65), .lt(comparator_28_lt));  // open: gt, eq
  and and_13 (and_13_out, comparator_28_lt, comparator_14_eq, comparator_29_gt);
  Comparator comparator_29 (.a(INVENTORY5p), .b(8'h60), .gt(comparator_29_gt));  // open: eq, lt
  food food_1 (.FOOD(multiplexer_2_out), .GIVEHP(food_1_givehp));
  Multiplexer #(.select(3), .width(8), .enable("false")) multiplexer_2 (
    .in0(INVENTORY1p), .in1(INVENTORY2p), .in2(INVENTORY3p), .in3(INVENTORY4p), .in4(INVENTORY5p),
    .out(multiplexer_2_out), .sel(bit_extender_1_out));  // open: in5, in6, in7
  Multiplexer #(.width(8), .enable("false")) multiplexer_3 (
    .in0(NewPLyOM), .in1(maps_1_ypp), .out(multiplexer_3_out), .sel(gS0));
  Register Ypp (.D(multiplexer_3_out), .Q(PLyOM), .clk(or_4_out));  // open: en, clr
  or or_4 (or_4_out, changePCy, LoadMap);
  maps maps_1 (
    .Map_No(mapLevelCur), .Addr_on_map(mapSTelemREAD), .DATA(mapSTDATAreaded), .Xpp(maps_1_xpp),
    .Ypp(maps_1_ypp), .Width(maps_1_width), .Height(maps_1_height));  // open: LEN
  Register #(.width(12)) u_mapH (.D(maps_1_height), .Q(MapH), .clk(LoadMap));  // open: en, clr
  // Probe on InpKey
  Comparator comparator_30 (.a(p_x_y_1_t), .b(8'h23), .eq(comparator_30_eq));  // open: gt, lt
  not not_1 (not_1_out, comparator_30_eq);
  and and_14 (and_14_out, not_1_out, WonInp, comparator_15_eq);
  not not_2 (not_2_out, comparator_31_eq);
  Comparator comparator_31 (.a(p_x_y_1), .b(8'h23), .eq(comparator_31_eq));  // open: gt, lt
  and and_15 (and_15_out, not_2_out, WonInp, comparator_16_eq);
  not not_3 (not_3_out, comparator_32_eq);
  Comparator comparator_32 (.a(p_x_1_y), .b(8'h23), .eq(comparator_32_eq));  // open: gt, lt
  and and_16 (and_16_out, not_3_out, WonInp, comparator_17_eq);
  Comparator comparator_33 (.a(p_x_1_y_t), .b(8'h23), .eq(comparator_33_eq));  // open: gt, lt
  not not_4 (not_4_out, comparator_33_eq);
  and and_17 (and_17_out, not_4_out, WonInp, comparator_18_eq);
  quick quick_8 (.IN(and_9_out), .OUT(itemRES1));
  quick quick_9 (.IN(and_10_out), .OUT(itemRES2));
  quick quick_10 (.IN(and_11_out), .OUT(itemRES3));
  or or_5 (CHHPinmove, and_9_out, and_10_out, and_11_out, and_12_out, and_13_out);
  quick quick_11 (.IN(and_12_out), .OUT(itemRES4));
  quick quick_12 (.IN(and_13_out), .OUT(itemRES5));
  Adder adder_2 (.a(food_1_givehp), .b(playerHPCUR), .out(adder_2_out));  // open: cin, cout
  Pull_Resistor pull_resistor_1 (.node(pull_resistor_1_node));
  Comparator comparator_34 (.a(adder_2_out), .b(8'h32), .eq(pull_resistor_1_node));  // open: gt, lt
  Comparator comparator_35 (.a(InpKey), .b(8'h61), .eq(comparator_35_eq));  // open: gt, lt
  Comparator comparator_36 (.a(InpKey), .b(8'h64), .eq(comparator_36_eq));  // open: gt, lt
  Comparator comparator_37 (.a(InpKey), .b(8'h77), .eq(WonInp));  // open: gt, lt
  Comparator comparator_38 (.a(InpKey), .b(8'h71), .eq(comparator_38_eq));  // open: gt, lt
  quick quick_13 (.IN(comparator_38_eq), .OUT(qres));
  Subtractor subtractor_2 (.a(PLyOM), .b(8'h1), .out(subtractor_2_out));  // open: bin, bout
  Adder adder_3 (.a(PLyOM), .b(8'h1), .out(adder_3_out));  // open: cin, cout
  Adder adder_4 (.a(PLxOM), .b(8'h1), .out(adder_4_out));  // open: cin, cout
  Subtractor subtractor_3 (.a(PLxOM), .b(8'h1), .out(subtractor_3_out));  // open: bin, bout
  Register register_2 (.D(p_x_y), .Q(INVENTORY1), .clk(INV1ch), .clr(or_6_out));  // open: en
  or or_6 (or_6_out, mainRES, itemRES1);
  Register register_3 (.D(p_x_y), .Q(INVENTORY2), .clk(INV2ch), .clr(or_7_out));  // open: en
  or or_7 (or_7_out, mainRES, itemRES2);
  Register register_4 (.D(p_x_y), .Q(INVENTORY3), .clk(INV3ch), .clr(or_8_out));  // open: en
  or or_8 (or_8_out, mainRES, itemRES3);
  Register register_5 (.D(p_x_y), .Q(INVENTORY4), .clk(INV4ch), .clr(or_9_out));  // open: en
  or or_9 (or_9_out, mainRES, itemRES4);
  Register register_6 (.D(p_x_y), .Q(INVENTORY5), .clk(INV5ch), .clr(or_10_out));  // open: en
  or or_10 (or_10_out, mainRES, itemRES5);
  Multiplexer #(.width(8), .enable("false")) multiplexer_4 (
    .in0(adder_2_out), .in1(8'h32), .out(multiplexer_4_out), .sel(pull_resistor_1_node));
  and and_18 (and_18_out, or_11_out, CHHPinmove);
  or or_11 (or_11_out, InpFlpre, ATCInpFlpre);
  Register register_7 (.D(NewMapLevelCh), .Q(mapLevelCur), .clk(MapLevelCh), .clr(mainRES));  // open: en
  Register register_8 (.D(NewPlayerHP), .Q(playerHPCUR), .clk(buffer_1_out), .clr(mainRES));  // open: en
  buf buffer_1 (buffer_1_out, PLAYERHPCH);
  Pull_Resistor pull_resistor_2 (.node(buffer_1_out));
  not not_5 (not_5_out, InpFlmove1);
  or or_12 (InpFlmove1, comparator_35_eq, comparator_36_eq);
  not not_6 (not_6_out, not_5_out);
  assign NewPLyOM = and_14_out ? subtractor_2_out : 8'bz;  // Controlled_Buffer controlled_buffer_1
  assign NewPLyOM = and_15_out ? adder_3_out : 8'bz;  // Controlled_Buffer controlled_buffer_2
  assign NewPLxOM = and_16_out ? adder_4_out : 8'bz;  // Controlled_Buffer controlled_buffer_3
  assign NewPLxOM = and_17_out ? subtractor_3_out : 8'bz;  // Controlled_Buffer controlled_buffer_4
  assign MAP_tospace_ELEM = mapPREst1 ? p_x_y__elemOnMap : 12'bz;  // Controlled_Buffer controlled_buffer_5
  quick quick_14 (.IN(mapPREst1), .OUT(stMapCLC1));
  or or_13 (mapPREst1, InpFlmove31, InpFlmove32, InpFlmove33, InpFlmove34, InpFlmove35);
  assign NewPlayerHP = and_18_out ? multiplexer_4_out : 8'bz;  // Controlled_Buffer controlled_buffer_6
  assign PLAYERHPCH = and_18_out ? 1'b1 : 1'bz;  // Controlled_Buffer controlled_buffer_7
  Clock clock_1 (.out(mainClk));
  Button button_1 (.out(button_1_out));
  or or_14 (mainRES, button_1_out, qres);
  Adder #(.width(2)) adder_5 (.a(PlDir), .b(2'b01), .out(adder_5_out));  // open: cin, cout
  Multiplexer #(.width(2), .enable("false")) multiplexer_5 (
    .in0(adder_5_out), .in1(subtractor_4_out), .out(NewPlDir), .sel(comparator_35_eq));
  Subtractor #(.width(2)) subtractor_4 (.a(PlDir), .b(2'b01), .out(subtractor_4_out));  // open: bin, bout
  quick quick_15 (.IN(not_6_out), .OUT(PlDirCh));
  or or_15 (or_15_out, and_14_out, and_15_out);
  or or_16 (or_16_out, and_16_out, and_17_out);
  Comparator #(.width(2)) comparator_39 (.a(2'b00), .b(ATACK_MODE), .eq(gS0));  // open: gt, lt
  Comparator #(.width(2)) comparator_40 (.a(2'b01), .b(ATACK_MODE), .eq(gS1));  // open: gt, lt
  Comparator #(.width(2)) comparator_41 (.a(2'b10), .b(ATACK_MODE), .eq(gS2));  // open: gt, lt
  Register #(.width(2)) register_9 (.D(gSto), .Q(ATACK_MODE), .clk(buffer_2_out), .clr(mainRES));  // open: en
  buf buffer_2 (buffer_2_out, StateCh);
  Pull_Resistor pull_resistor_3 (.node(buffer_2_out));
  Register #(.width(2)) register_10 (.D(NewPlDir), .Q(PlDir), .clk(PlDirCh), .clr(mainRES));  // open: en
  quick quick_16 (.IN(or_15_out), .OUT(changePCy));
  or or_17 (InpFlmove2, or_15_out, or_16_out);
  quick quick_17 (.IN(or_16_out), .OUT(changePCx));
  Register register_11 (.D(INVENTORY1), .Q(INVENTORY1p), .clk(invchn));  // open: en, clr
  Register register_12 (.D(INVENTORY2), .Q(INVENTORY2p), .clk(invchn));  // open: en, clr
  Register register_13 (.D(INVENTORY3), .Q(INVENTORY3p), .clk(invchn));  // open: en, clr
  Register register_14 (.D(INVENTORY4), .Q(INVENTORY4p), .clk(invchn));  // open: en, clr
  Register register_15 (.D(INVENTORY5), .Q(INVENTORY5p), .clk(invchn));  // open: en, clr
  assign NewPlayerHP = LoadMap ? 8'ha : 8'bz;  // Controlled_Buffer controlled_buffer_8
  buf buffer_3 (LoadMap, and_19_out);
  and and_19 (and_19_out, InpFlpreSTRT, gS0);
  quick quick_18 (.IN(chGM), .OUT(quick_18_out));
  Register #(.width(4)) register_16 (.D(adder_6_out), .Q(register_16_q), .clk(and_20_out), .clr(invchn));  // open: en
  and and_20 (and_20_out, or_20_out, mainClk);
  or or_18 (invchn, InpFlpreAtc, \InpFlpreС );
  or or_19 (or_19_out, and_19_out, quick_18_out);
  assign StateCh = or_19_out ? or_19_out : 1'bz;  // Controlled_Buffer controlled_buffer_9
  Adder #(.width(4)) adder_6 (.a(4'b0001), .b(register_16_q), .out(adder_6_out));  // open: cin, cout
  Comparator #(.width(4)) comparator_42 (
    .a(4'b1001), .b(register_16_q), .gt(comparator_42_gt), .eq(comparator_42_eq), .lt(comparator_42_lt));
  Comparator #(.width(4)) comparator_43 (.a(register_16_q), .b(4'b0010), .eq(comparator_43_eq));  // open: gt, lt
  Comparator #(.width(4)) comparator_44 (.a(register_16_q), .b(4'b0011), .eq(comparator_44_eq));  // open: gt, lt
  Comparator #(.width(4)) comparator_45 (.a(register_16_q), .b(4'b0011), .eq(comparator_45_eq));  // open: gt, lt
  Comparator #(.width(4)) comparator_46 (.a(register_16_q), .b(4'b0100), .eq(comparator_46_eq));  // open: gt, lt
  Comparator #(.width(4)) comparator_47 (.a(register_16_q), .b(4'b0100), .eq(comparator_47_eq));  // open: gt, lt
  Comparator #(.width(4)) comparator_48 (.a(register_16_q), .b(4'b0101), .eq(comparator_48_eq));  // open: gt, lt
  Comparator #(.width(4)) comparator_49 (.a(register_16_q), .b(4'b0101), .eq(comparator_49_eq));  // open: gt, lt
  Comparator #(.width(4)) comparator_50 (.a(register_16_q), .b(4'b0110), .eq(comparator_50_eq));  // open: gt, lt
  Comparator #(.width(4)) comparator_51 (.a(register_16_q), .b(4'b0110), .eq(comparator_51_eq));  // open: gt, lt
  Comparator #(.width(4)) comparator_52 (.a(register_16_q), .b(4'b0111), .eq(comparator_52_eq));  // open: gt, lt
  Adder adder_7 (.a(PLyOM), .b(8'h1), .out(adder_7_out));  // open: cin, cout
  Adder adder_8 (.a(PLxOM), .b(8'h1), .out(adder_8_out));  // open: cin, cout
  assign PLAYERHPCH = quick_19_out ? quick_19_out : 1'bz;  // Controlled_Buffer controlled_buffer_10
  quick quick_19 (.IN(or_19_out), .OUT(quick_19_out));
  Multiplexer #(.select(2), .width(2), .enable("false")) multiplexer_6 (
    .in0(2'b01), .in1(2'b10), .in2(2'b01), .out(gSto), .sel({gS2, gS1}));  // open: in3
  Multiplexer #(.select(2), .width(8), .enable("false")) multiplexer_7 (
    .in0(8'h1f), .in1({8{1'b0}}), .in2(8'h1e), .out(gStdtScrMem), .sel({gS2, gS1}));  // open: in3
  or or_20 (or_20_out, comparator_42_gt, comparator_42_lt);
  x_y__to_memory_elem_number x_y_____elem (.H(MapW), .Y(PLyOM), .X(PLxOM), .ELEM(p_x_y__elemOnMap), .START(12'h4));
  x_y__to_memory_elem_number x_y_____elem_2 (
    .H(MapW), .Y(adder_7_out), .X(PLxOM), .ELEM(p_x_y_1__elemOnMap), .START(12'h4));
  x_y__to_memory_elem_number x_y_____elem_3 (
    .H(MapW), .Y(PLyOM), .X(adder_8_out), .ELEM(p_x_1_y__elemOnMap), .START(12'h4));
  Lquick lquick_1 (.IN(comparator_42_eq), .OUT(InpFlpre), .CLC(mainClk));
  assign MAP_tospace_ELEM = comparator_43_eq ? p_x_y__elemOnMap : 12'bz;  // Controlled_Buffer controlled_buffer_11
  Register register_17 (.D(objectONmap), .Q(p_x_y), .clk(comparator_44_eq));  // open: en, clr
  assign MAP_tospace_ELEM = comparator_45_eq ? p_x_y_1__elemOnMap_t : 12'bz;  // Controlled_Buffer controlled_buffer_12
  Register register_18 (.D(objectONmap), .Q(p_x_y_1_t), .clk(comparator_46_eq));  // open: en, clr
  assign MAP_tospace_ELEM = comparator_47_eq ? p_x_y_1__elemOnMap : 12'bz;  // Controlled_Buffer controlled_buffer_13
  Register register_19 (.D(objectONmap), .Q(p_x_y_1), .clk(comparator_48_eq));  // open: en, clr
  assign MAP_tospace_ELEM = comparator_49_eq ? p_x_1_y__elemOnMap_t : 12'bz;  // Controlled_Buffer controlled_buffer_14
  Register register_20 (.D(objectONmap), .Q(p_x_1_y_t), .clk(comparator_50_eq));  // open: en, clr
  assign MAP_tospace_ELEM = comparator_51_eq ? p_x_1_y__elemOnMap : 12'bz;  // Controlled_Buffer controlled_buffer_15
  Register register_21 (.D(objectONmap), .Q(p_x_1_y), .clk(comparator_52_eq));  // open: en, clr
  Register #(.width(2)) register_22 (.D(ATCnewEN), .Q(ATCcurEN), .clk(ATCnewENclc));  // open: en, clr
  Comparator comparator_53 (.a(ATCInpKey), .b(8'h31), .eq(comparator_53_eq));  // open: gt, lt
  Comparator comparator_54 (.a(ATCInpKey), .b(8'h32), .eq(comparator_54_eq));  // open: gt, lt
  Comparator comparator_55 (.a(ATCInpKey), .b(8'h33), .eq(comparator_55_eq));  // open: gt, lt
  Comparator comparator_56 (.a(ATCInpKey), .b(8'h34), .eq(comparator_56_eq));  // open: gt, lt
  Comparator comparator_57 (.a(ATCInpKey), .b(8'h35), .eq(comparator_57_eq));  // open: gt, lt
  Subtractor subtractor_5 (.a(ATCInpKey), .b(8'h31), .out(subtractor_5_out));  // open: bin, bout
  Subtractor subtractor_6 (.a(PLyOM), .b(8'h1), .out(subtractor_6_out));  // open: bin, bout
  Subtractor subtractor_7 (.a(PLxOM), .b(8'h1), .out(subtractor_7_out));  // open: bin, bout
  Comparator comparator_58 (.a(INVENTORY1p), .b(8'h6b), .lt(comparator_58_lt));  // open: gt, eq
  Comparator comparator_59 (.a(INVENTORY1p), .b(8'h65), .gt(comparator_59_gt));  // open: eq, lt
  Comparator comparator_60 (.a(INVENTORY2p), .b(8'h6b), .lt(comparator_60_lt));  // open: gt, eq
  Comparator comparator_61 (.a(INVENTORY2p), .b(8'h65), .gt(comparator_61_gt));  // open: eq, lt
  Comparator comparator_62 (.a(INVENTORY3p), .b(8'h6b), .lt(comparator_62_lt));  // open: gt, eq
  Comparator comparator_63 (.a(INVENTORY3p), .b(8'h65), .gt(comparator_63_gt));  // open: eq, lt
  Comparator comparator_64 (.a(INVENTORY4p), .b(8'h6b), .lt(comparator_64_lt));  // open: gt, eq
  Comparator comparator_65 (.a(INVENTORY4p), .b(8'h65), .gt(comparator_65_gt));  // open: eq, lt
  Comparator comparator_66 (.a(INVENTORY5p), .b(8'h6b), .lt(comparator_66_lt));  // open: gt, eq
  Comparator comparator_67 (.a(INVENTORY5p), .b(8'h65), .gt(comparator_67_gt));  // open: eq, lt
  Multiplexer #(.select(3), .width(8), .enable("false")) multiplexer_8 (
    .in0(INVENTORY1p), .in1(INVENTORY2p), .in2(INVENTORY3p), .in3(INVENTORY4p), .in4(INVENTORY5p),
    .out(multiplexer_8_out), .sel(bit_extender_2_out));  // open: in5, in6, in7
  Bit_Extender #(.out_width(3)) bit_extender_2 (.in(subtractor_5_out), .out(bit_extender_2_out));
  Comparator #(.width(2)) comparator_68 (.a(PlDir), .b(2'b00), .eq(comparator_68_eq));  // open: gt, lt
  Comparator #(.width(2)) comparator_69 (.a(PlDir), .b(2'b10), .eq(comparator_69_eq));  // open: gt, lt
  Comparator #(.width(2)) comparator_70 (.a(PlDir), .b(2'b01), .eq(comparator_70_eq));  // open: gt, lt
  Comparator #(.width(2)) comparator_71 (.a(PlDir), .b(2'b11), .eq(comparator_71_eq));  // open: gt, lt
  x_y__to_memory_elem_number x_y_____elem_4 (
    .H(MapW), .Y(subtractor_6_out), .X(PLxOM), .ELEM(p_x_y_1__elemOnMap_t), .START(12'h4));
  x_y__to_memory_elem_number x_y_____elem_5 (
    .H(MapW), .Y(PLyOM), .X(subtractor_7_out), .ELEM(p_x_1_y__elemOnMap_t), .START(12'h4));
  Register register_23 (.D(ENDMGst), .Q(ENDMG), .clk(ATCinit));  // open: en, clr
  Register register_24 (.D(ENHPst), .Q(ENHP), .clk(or_21_out));  // open: en, clr
  or or_21 (or_21_out, ATCnEhp, ATCinit);
  and and_21 (and_21_out, comparator_58_lt, comparator_53_eq, comparator_59_gt);
  and and_22 (and_22_out, comparator_60_lt, comparator_54_eq, comparator_61_gt);
  and and_23 (and_23_out, comparator_62_lt, comparator_55_eq, comparator_63_gt);
  or or_22 (ATCinisW, and_21_out, and_22_out, and_23_out, and_24_out, and_25_out);
  and and_24 (and_24_out, comparator_64_lt, comparator_56_eq, comparator_65_gt);
  and and_25 (and_25_out, comparator_66_lt, comparator_57_eq, comparator_67_gt);
  Pull_Resistor pull_resistor_4 (.node(pull_resistor_4_node));
  weapon weapon_1 (.WEAPON(multiplexer_8_out), .DMG(weapon_1_dmg));
  Comparator comparator_72 (
    .a(weapon_1_dmg), .b(ENHP), .gt(pull_resistor_4_node), .eq(comparator_72_eq), .lt(comparator_72_lt));
  Comparator comparator_73 (.a(p_x_y_1_t), .b(8'h30), .gt(comparator_73_gt));  // open: eq, lt
  Comparator comparator_74 (.a(p_x_y_1), .b(8'h30), .gt(comparator_74_gt));  // open: eq, lt
  Comparator comparator_75 (.a(p_x_1_y), .b(8'h30), .gt(comparator_75_gt));  // open: eq, lt
  Comparator comparator_76 (.a(p_x_1_y_t), .b(8'h30), .gt(comparator_76_gt));  // open: eq, lt
  Multiplexer #(.width(8), .enable("false")) multiplexer_9 (
    .in0(8'h20), .in1(mapSTDATAreaded), .out(multiplexer_9_out), .sel(not_8_out));
  or or_23 (ATCpWIN, pull_resistor_4_node, comparator_72_eq);
  Pull_Resistor pull_resistor_5 (.node(comparator_72_eq));
  Pull_Resistor pull_resistor_6 (.node(comparator_72_lt));
  assign ENHPst = and_29_out ? subtractor_8_out : 8'bz;  // Controlled_Buffer controlled_buffer_16
  Subtractor subtractor_8 (.a(ENHP), .b(weapon_1_dmg), .out(subtractor_8_out));  // open: bin, bout
  Comparator comparator_77 (.a(p_x_y_1_t), .b(8'h35), .lt(comparator_77_lt));  // open: gt, eq
  Comparator comparator_78 (.a(p_x_y_1), .b(8'h35), .lt(comparator_78_lt));  // open: gt, eq
  Comparator comparator_79 (.a(p_x_1_y), .b(8'h35), .lt(comparator_79_lt));  // open: gt, eq
  Comparator comparator_80 (.a(p_x_1_y_t), .b(8'h35), .lt(comparator_80_lt));  // open: gt, eq
  Multiplexer #(.width(12), .enable("false")) multiplexer_10 (
    .in0(MAP_tospace_ELEM), .in1(mapSTelemREAD), .out(multiplexer_10_out), .sel(not_8_out));
  and and_26 (and_26_out, not_8_out, mainClk);
  and and_27 (and_27_out, InpFl1, gS1);
  or or_24 (out_1, and_27_out, and_28_out);
  and and_28 (and_28_out, 1'b0, gS2);
  // Probe on playerHPCUR
  assign StateCh = ATCpWIN ? ATCpWIN : 1'bz;  // Controlled_Buffer controlled_buffer_17
  and and_29 (and_29_out, ATCinisW, comparator_72_lt);
  quick quick_20 (.IN(and_29_out), .OUT(ATCnEhp));
  assign MAP_tospace_ELEM = and_30_out ? p_x_y_1__elemOnMap_t : 12'bz;  // Controlled_Buffer controlled_buffer_18
  assign ATCnewEN = and_30_out ? bit_extender_3_out : 2'bz;  // Controlled_Buffer controlled_buffer_19
  Bit_Extender #(.out_width(2)) bit_extender_3 (.in(subtractor_9_out), .out(bit_extender_3_out));
  Subtractor subtractor_9 (.a(p_x_y_1_t), .b(8'h31), .out(subtractor_9_out));  // open: bin, bout
  and and_30 (and_30_out, comparator_73_gt, comparator_77_lt, comparator_68_eq);
  and and_31 (and_31_out, comparator_74_gt, comparator_78_lt, comparator_69_eq);
  and and_32 (and_32_out, comparator_75_gt, comparator_79_lt, comparator_70_eq);
  and and_33 (and_33_out, comparator_76_gt, comparator_80_lt, comparator_71_eq);
  assign ATCnewEN = and_33_out ? bit_extender_4_out : 2'bz;  // Controlled_Buffer controlled_buffer_20
  Subtractor subtractor_10 (.a(p_x_1_y_t), .b(8'h31), .out(subtractor_10_out));  // open: bin, bout
  Bit_Extender #(.out_width(2)) bit_extender_4 (.in(subtractor_10_out), .out(bit_extender_4_out));
  assign MAP_tospace_ELEM = and_33_out ? p_x_1_y__elemOnMap_t : 12'bz;  // Controlled_Buffer controlled_buffer_21
  Register #(.width(12)) register_25 (.D(adder_9_out), .Q(mapSTelemREAD), .clk(and_26_out), .clr(mainRES));  // open: en
  Adder #(.width(12)) adder_9 (.a(mapSTelemREAD), .b(12'h1), .out(adder_9_out));  // open: cin, cout
  graphic_elems graphic_elems_1 (.ADDR(gStdtScrMem), .ELEM(memN), .DATA(graphic_elems_1_data), .LEN(tpLen));
  // Probe on gStdtScrMem
  or or_25 (memReadyToPrint, button_2_out, quick_21_out);
  Button button_2 (.out(button_2_out));
  quick quick_21 (.IN(out_1), .OUT(quick_21_out));
  not not_7 (not_7_out, ATCnewENclc);
  or or_26 (ATCnewENclc, and_30_out, and_31_out, and_32_out, and_33_out);
  assign StateCh = ATCnewENclc ? ATCnewENclc : 1'bz;  // Controlled_Buffer controlled_buffer_22
  RAM #(.addrWidth(12), .bus("separate")) ram_1 (
    .addr(multiplexer_10_out), .din(multiplexer_9_out), .data(objectONmap), .str(mapPREst), .clk(stMapCLC));  // open: sel, ld, clr
  not not_8 (not_8_out, comparator_81_eq);
  Comparator #(.width(12)) comparator_81 (.a(mapSTelemREAD), .b(12'h94), .eq(comparator_81_eq));  // open: gt, lt
  or or_27 (stMapCLC, and_26_out, stMapCLC2, stMapCLC1);
  not not_9 (not_9_out, printing_map_1_cond_of_change);
  printing_map printing_map_1 (
    .Xpp(PLxOM), .Ypp(PLyOM), .Clock(mainClk), .Mem_N(memN), .Cond_of_change(printing_map_1_cond_of_change),
    .No_of_map(mapLevelCur), .Char_on_screen(printing_map_1_char_on_screen), .Num_of_elem(gStdtScrMem),
    .Main_Res(quick_21_out));
  Register #(.width(1)) register_26 (
    .D(adder_10_out), .Q(register_26_q), .clk(and_34_out), .clr(ATCnewENclc));  // open: en
  and and_34 (and_34_out, ATCinit, mainClk);
  assign MAP_tospace_ELEM = and_31_out ? p_x_y_1__elemOnMap : 12'bz;  // Controlled_Buffer controlled_buffer_23
  Subtractor subtractor_11 (.a(p_x_y_1), .b(8'h31), .out(subtractor_11_out));  // open: bin, bout
  assign ATCnewEN = and_31_out ? bit_extender_5_out : 2'bz;  // Controlled_Buffer controlled_buffer_24
  Bit_Extender #(.out_width(2)) bit_extender_5 (.in(subtractor_11_out), .out(bit_extender_5_out));
  not not_10 (not_10_out, not_11_out);
  not not_11 (not_11_out, not_7_out);
  not not_12 (stMapCLC2, not_10_out);
  Bit_Extender #(.out_width(2)) bit_extender_6 (.in(subtractor_12_out), .out(bit_extender_6_out));
  assign ATCnewEN = and_32_out ? bit_extender_6_out : 2'bz;  // Controlled_Buffer controlled_buffer_25
  Subtractor subtractor_12 (.a(p_x_1_y), .b(8'h31), .out(subtractor_12_out));  // open: bin, bout
  assign MAP_tospace_ELEM = and_32_out ? p_x_1_y__elemOnMap : 12'bz;  // Controlled_Buffer controlled_buffer_26
  or or_28 (mapPREst, not_8_out, ATCnewENclc, mapPREst1);
  assign memChar = not_9_out ? graphic_elems_1_data : 8'bz;  // Controlled_Buffer controlled_buffer_27
  assign memChar = printing_map_1_cond_of_change ? printing_map_1_char_on_screen : 8'bz;  // Controlled_Buffer controlled_buffer_28
  Adder #(.width(1)) adder_10 (.a(register_26_q), .b(1'b1), .out(adder_10_out));  // open: cin, cout
  not not_13 (not_13_out, comparator_82_eq);
  Comparator #(.width(1)) comparator_82 (.a(register_26_q), .b(1'b1), .eq(comparator_82_eq));  // open: gt, lt
  enemies enemies_1 (
    .ADDR(ATCcurEN), .ELEMIm(ENIMN), .ELEMNm(ENIMN), .Img(ENimgChrst), .Txt(ENNmChrst), .HP(enemies_1_hp),
    .DMG(ENDMGst));
  quick quick_22 (.IN(ATCnewENclc), .OUT(InpFlpreAtc));
  assign ATCinit = not_13_out ? not_13_out : 1'bz;  // Controlled_Buffer controlled_buffer_29
  Pull_Resistor pull_resistor_7 (.node(ATCinit));
  assign ENHPst = not_13_out ? enemies_1_hp : 8'bz;  // Controlled_Buffer controlled_buffer_30

  // Other names for the same wires on the sheet: ATCinit1 = ATCinit; gameState[1:0] = ATACK_MODE;
  //   mapPREst2 = ATCnewENclc; p_x_y_obj[7:0] = objectONmap

  // Notes on the sheet:
  //   inp: 1
  //   inp: 2
  //   inp: 3
  //   inp: 4
  //   inp: 5
  //   its eat in cell
  //   its weapon in cell
  //   inp: 1
  //   inp: 2
  //   inp: 3
  //   inp: 4
  //   inp: 5
  //   EAT FOOD
  //   LOAD MAP
  //   INVENTORY
  //   item теряется если взять вместо него
  //   MOVE PART
  //   inp: a
  //   inp: d
  //   inp: w
  //   inp: q
  //   REMOVE ITEM FROM GAME MAP
  //   Curent map level
  //   Player HP
  //   INVENTORY REGISTERS
  //   GAME GLOBAL VARIBLES
  //   0
  //   3
  //   ->
  //   1
  //   2
  //   Game state
  //   0 - start screen 1 - walking 2 - atack
  //   Player Direction
  //   Player (y+1,x) cell
  //   Player (y,x+1) cell
  //   MOVE INIT
  //   Player cell
  //   ATC MOVE
  //   inp: 1
  //   inp: 2
  //   inp: 3
  //   inp: 4
  //   inp: 5
  //   Current Enemy number
  //   Player (y-1,x) cell
  //   Player (y,x-1) cell
  //   Current Enemy dmg
  //   Current Enemy hp
  //   MEET ENEMY AND CHANGE GAME MODE TO ATACK
  //   MAP
  //   ENEMY INIT
endmodule

// CP
module consoler (
  input  [7:0] MEM_D,
  input  CLK,
  input  [11:0] PRINT_SIZE,
  input  RESET,
  output IT_WORKED,
  output [7:0] INPUT_CHAR,
  output [11:0] MEM_A
);

  wire adder_1_out, and_3_out, and_4_out, clc, comparator_1_eq, not_1_out, not_2_out, not_3_out, not_4_out,
       not_5_out, or_1_out, PRND, readConsole, register_1_q, register_2_q, RES, RESET_MEMORY_COUNTER_out,
       uart_1_p3, uart_1_p6, uart_1_p8;
  wire [7:0] uart_1_p1;
  wire [11:0] adder_2_out;

  and and_1 (IT_WORKED, not_2_out, PRND, register_1_q);
  Register #(.width(1)) register_1 (.D(adder_1_out), .Q(register_1_q), .clk(or_1_out));  // open: en, clr
  or or_1 (or_1_out, RES, uart_1_p3);
  and and_2 (clc, CLK, not_1_out);
  not not_1 (not_1_out, RES);
  not not_2 (not_2_out, uart_1_p3);
  Adder #(.width(1)) adder_1 (.a(register_1_q), .b(1'b1), .out(adder_1_out));  // open: cin, cout
  not not_3 (not_3_out, RESET);
  and and_3 (and_3_out, clc, comparator_1_eq);
  Register #(.width(1)) register_2 (.D(RESET), .Q(register_2_q), .clk(RESET), .clr(not_4_out));  // open: en
  not not_4 (not_4_out, not_3_out);
  Register register_3 (.D(uart_1_p1), .Q(INPUT_CHAR), .clk(and_3_out), .clr(RES));  // open: en
  or or_2 (RES, register_2_q, RESET_MEMORY_COUNTER_out);
  Button RESET_MEMORY_COUNTER (.out(RESET_MEMORY_COUNTER_out));
  Comparator comparator_1 (.a(INPUT_CHAR), .b({8{1'b0}}), .eq(comparator_1_eq));  // open: gt, lt
  not not_5 (not_5_out, PRND);
  Register #(.width(12)) register_4 (.D(adder_2_out), .Q(MEM_A), .clk(and_4_out), .clr(RES));  // open: en
  not not_6 (readConsole, PRND);
  and and_4 (and_4_out, not_5_out, clc);
  // UART uart_1: pin names not known; wires that end beside it: uart_1_p1, MEM_D, uart_1_p3, clc, uart_1_p3, uart_1_p6, uart_1_p6, uart_1_p8
  Adder #(.width(12)) adder_2 (.a(MEM_A), .b(12'h1), .out(adder_2_out));  // open: cin, cout
  or or_3 (uart_1_p8, uart_1_p3, readConsole);
  Comparator #(.width(12)) comparator_2 (.a(MEM_A), .b(PRINT_SIZE), .eq(PRND));  // open: gt, lt

  // Notes on the sheet:
  //   Input writened
  //   12 бит адрес
  //   Frame Printed
  //   Print Frame
  //   A - Адрес к каторому обращается
  //   B - элемент по адресу
endmodule

// GE
module graphic_elems (
  input  [7:0] ADDR,
  input  [11:0] ELEM,
  output [7:0] DATA,
  output [11:0] LEN
);

  wire [7:0] deMux1, geD0, geD1, geD2, geD2_0, geD2_1, geD3, geD4, geD5, geD6, geD7, geD8, geD9, geD10,
       geD11, geD12, geD13, geD14, geD15;
  wire [11:0] deMuxl1;

  ROM #(.addrWidth(12)) rom_1 (.addr(ELEM), .data(geD0));  // open: sel
  ROM #(.addrWidth(12)) rom_2 (.addr(ELEM), .data(geD1));  // open: sel
  ROM #(.addrWidth(12)) rom_3 (.addr(ELEM), .data(geD2));  // open: sel
  ROM #(.addrWidth(12)) rom_4 (.addr(ELEM), .data(geD3));  // open: sel
  ROM #(.addrWidth(12)) rom_5 (.addr(ELEM), .data(geD4));  // open: sel
  ROM #(.addrWidth(12)) rom_6 (.addr(ELEM), .data(geD5));  // open: sel
  ROM #(.addrWidth(12)) rom_7 (.addr(ELEM), .data(geD6));  // open: sel
  ROM #(.addrWidth(12)) rom_8 (.addr(ELEM), .data(geD7));  // open: sel
  ROM #(.addrWidth(12)) rom_9 (.addr(ELEM), .data(geD8));  // open: sel
  ROM #(.addrWidth(12)) rom_10 (.addr(ELEM), .data(geD9));  // open: sel
  ROM #(.addrWidth(12)) rom_11 (.addr(ELEM), .data(geD10));  // open: sel
  ROM #(.addrWidth(12)) rom_12 (.addr(ELEM), .data(geD11));  // open: sel
  ROM #(.addrWidth(12)) rom_13 (.addr(ELEM), .data(geD12));  // open: sel
  ROM #(.addrWidth(12)) rom_14 (.addr(ELEM), .data(geD13));  // open: sel
  ROM #(.addrWidth(12)) rom_15 (.addr(ELEM), .data(geD14));  // open: sel
  ROM #(.addrWidth(12)) rom_16 (.addr(ELEM), .data(geD15));  // open: sel
  ROM #(.addrWidth(12)) rom_17 (.addr(ELEM), .data(geD2_0));  // open: sel
  ROM #(.addrWidth(12)) rom_18 (.addr(ELEM), .data(geD2_1));  // open: sel
  Multiplexer #(.select(5), .width(8), .enable("false")) multiplexer_1 (
    .in0(geD0), .in1(geD1), .in2(geD2), .in3(geD3), .in4(geD4), .in5(geD5), .in6(geD6), .in7(geD7),
    .in8(geD8), .in9(geD9), .in10(geD10), .in11(geD11), .in12(geD12), .in13(geD13), .in14(geD14),
    .in15(geD15), .in30(geD2_1), .in31(geD2_0), .out(deMux1), .sel(ADDR[4:0]));  // open: in16, in17, in18, in19, in20, in21, in22, in23, in24, in25, in26, in27, in28, in29
  Multiplexer #(.select(5), .width(12), .enable("false")) multiplexer_2 (
    .in0(12'had5), .in1(12'h596), .in2(12'h596), .in3(12'h596), .in4(12'h596), .in5(12'h596), .in6(12'h596),
    .in7(12'h596), .in8(12'h596), .in9(12'h596), .in10(12'h596), .in11(12'h596), .in12(12'h596),
    .in13(12'h596), .in14(12'h596), .in15(12'h596), .in30(12'had5), .in31(12'had5), .out(deMuxl1),
    .sel(ADDR[4:0]));  // open: in16, in17, in18, in19, in20, in21, in22, in23, in24, in25, in26, in27, in28, in29
  Multiplexer #(.select(3), .width(8), .enable("false")) multiplexer_3 (
    .in0(deMux1), .out(DATA), .sel(ADDR[7:5]));  // open: in1, in2, in3, in4, in5, in6, in7
  Multiplexer #(.select(3), .width(12), .enable("false")) multiplexer_4 (
    .in0(deMuxl1), .out(LEN), .sel(ADDR[7:5]));  // open: in1, in2, in3, in4, in5, in6, in7

  // Other names for the same wires on the sheet: geAddr1[4:0] = ADDR[4:0]; geAddr2[2:0] = ADDR[7:5];
  //   geEl[11:0] = ELEM

  // Notes on the sheet:
  //   BOARD
  //   contents of rom_1 (hex, n*v repeats v):
  //   0 76*23 a 23 52*20 23 21*20 23 a 23 52*20 23 21*20 23 a 23 52*20 23 21*20 23 a 23 52*20 23 21*20 23
  //   a 23 52*20 23 21*20 23 a 23 52*20 23 21*20 23 a 23 52*20 23 21*20 23 a 23 52*20 23 21*20 23 a 23
  //   52*20 23 21*20 23 a 23 52*20 23 21*20 23 a 23 52*20 23 21*20 23 a 23 52*20 23 21*20 23 a 23 52*20 23
  //   21*20 23 a 23 52*20 23 21*20 23 a 23 52*20 23 21*20 23 a 23 52*20 23 21*20 23 a 23 52*20 23 21*20 23
  //   a 23 52*20 23 21*20 23 a 23 52*20 23 21*20 23 a 23 52*20 23 21*20 23 a 23 52*20 23 21*20 23 a 23
  //   52*20 23*23 a 23 52*20 23 21*20 23 a 23 52*20 23 21*20 23 a 23 52*20 23 21*20 23 a 23 52*20 23 21*20
  //   23 a 23 52*20 23 21*20 23 a 76*23 a 23 74*20 23 a 76*23 a 23 9*20 23 9*20 23 9*20 23 9*20 23 9*20 23
  //   20 48 50 20 7c 10*20 7c 28 20 20 2f 31 30 29 20 23 a 23 9*20 23 9*20 23 9*20 23 9*20 23 9*20 23 20
  //   53 54 20 7c 10*20 7c 28 20 20 2f 31 30 29 20 23 a 23 9*20 23 9*20 23 9*20 23 9*20 23 9*20 23 20 48
  //   47 20 7c 10*20 7c 28 20 20 2f 31 30 29 20 23 a 23 9*20 23 9*20 23 9*20 23 9*20 23 9*20 23 24*20 23 a
  //   76*23 a 52*20
  //   FFL
  //   contents of rom_2 (hex, n*v repeats v):
  //   0 51*20 a 52*20 a 52*20 a 9*20 34*5f 9*20 a 8*20 7c 34*23 7c 8*20 a 8*20 7c 34*23 7c 8*20 a 8*20 7c
  //   34*23 7c 8*20 a 8*20 7c 34*23 7c 8*20 a 8*20 7c 34*23 7c 8*20 a 8*20 7c 34*23 7c 8*20 a 8*20 7c
  //   34*23 7c 8*20 a 8*20 7c 34*23 7c 8*20 a 8*20 7c 34*23 7c 8*20 a 8*20 7c 34*23 7c 8*20 a 8*20 7c
  //   34*23 7c 8*20 a 8*20 7c 34*23 7c 8*20 a 8*20 7c 34*23 7c 8*20 a 8*20 7c 34*23 7c 8*20 a 8*20 7c
  //   34*23 7c 8*20 a 8*20 7c 34*23 7c 8*20 a 8*20 7c 34*23 7c 8*20 a 8*20 7c 34*23 7c 8*20 a 8*20 7c
  //   34*23 7c 8*20 a 52*20 a 52*20 a 52*20 a 52*20
  //   FFFL
  //   contents of rom_3 (hex, n*v repeats v):
  //   0 51*20 a 52*20 a 52*20 a 52*20 a 52*20 a 52*20 a 52*20 a 18*20 16*5f 18*20 a 17*20 7c 16*23 7c
  //   17*20 a 17*20 7c 16*23 7c 17*20 a 17*20 7c 16*23 7c 17*20 a 17*20 7c 16*23 7c 17*20 a 17*20 7c 16*23
  //   7c 17*20 a 17*20 7c 16*23 7c 17*20 a 17*20 7c 16*23 7c 17*20 a 17*20 7c 16*23 7c 17*20 a 17*20 7c
  //   16*23 7c 17*20 a 17*20 7c 16*23 7c 17*20 a 17*20 7c 16*23 7c 17*20 a 52*20 a 52*20 a 52*20 a 52*20 a
  //   52*20 a 52*20 a 52*20 a 52*20
  //   FFFFL
  //   contents of rom_4 (hex, n*v repeats v):
  //   0 51*20 a 52*20 a 52*20 a 52*20 a 52*20 a 52*20 a 52*20 a 52*20 a 52*20 a 52*20 a 24*20 4*5f 24*20 a
  //   23*20 7c 4*23 7c 23*20 a 23*20 7c 4*23 7c 23*20 a 23*20 7c 4*23 7c 23*20 a 23*20 7c 4*23 7c 23*20 a
  //   23*20 7c 4*23 7c 23*20 a 52*20 a 52*20 a 52*20 a 52*20 a 52*20 a 52*20 a 52*20 a 52*20 a 52*20 a
  //   52*20 a 52*20
  //   LFL
  //   contents of rom_5 (hex, n*v repeats v):
  //   0 5c 5f 49*20 a 23 23 5c 5f 48*20 a 4*23 5c 5f 46*20 a 6*23 5c 5f 44*20 a 8*23 7c 43*20 a 8*23 7c
  //   43*20 a 8*23 7c 43*20 a 8*23 7c 43*20 a 8*23 7c 43*20 a 8*23 7c 43*20 a 8*23 7c 43*20 a 8*23 7c
  //   43*20 a 8*23 7c 43*20 a 8*23 7c 43*20 a 8*23 7c 43*20 a 8*23 7c 43*20 a 8*23 7c 43*20 a 8*23 7c
  //   43*20 a 8*23 7c 43*20 a 8*23 7c 43*20 a 8*23 7c 43*20 a 8*23 7c 43*20 a 8*23 7c 43*20 a 6*23 2f
  //   45*20 a 4*23 2f 47*20 a 23 23 2f 49*20 a 2f 51*20
  //   LFFL
  //   contents of rom_6 (hex, n*v repeats v):
  //   0 51*20 a 52*20 a 52*20 a 8*5f 44*20 a 8*23 7c 43*20 a 8*23 7c 43*20 a 8*23 7c 43*20 a 8*23 7c 43*20
  //   a 8*23 7c 43*20 a 8*23 7c 43*20 a 8*23 7c 43*20 a 8*23 7c 43*20 a 8*23 7c 43*20 a 8*23 7c 43*20 a
  //   8*23 7c 43*20 a 8*23 7c 43*20 a 8*23 7c 43*20 a 8*23 7c 43*20 a 8*23 7c 43*20 a 8*23 7c 43*20 a 8*23
  //   7c 43*20 a 8*23 7c 43*20 a 8*23 7c 43*20 a 52*20 a 52*20 a 52*20 a 52*20
  //   LFFFL
  //   contents of rom_7 (hex, n*v repeats v):
  //   0 51*20 a 52*20 a 52*20 a 52*20 a 52*20 a 52*20 a 52*20 a 17*5f 35*20 a 17*23 7c 34*20 a 17*23 7c
  //   34*20 a 17*23 7c 34*20 a 17*23 7c 34*20 a 17*23 7c 34*20 a 17*23 7c 34*20 a 17*23 7c 34*20 a 17*23
  //   7c 34*20 a 17*23 7c 34*20 a 17*23 7c 34*20 a 17*23 7c 34*20 a 52*20 a 52*20 a 52*20 a 52*20 a 52*20
  //   a 52*20 a 52*20 a 52*20
  //   LFFFFL
  //   contents of rom_8 (hex, n*v repeats v):
  //   0 51*20 a 52*20 a 52*20 a 52*20 a 52*20 a 52*20 a 52*20 a 52*20 a 52*20 a 52*20 a 18*20 5*5f 29*20 a
  //   17*20 7c 5*23 7c 28*20 a 17*20 7c 5*23 7c 28*20 a 17*20 7c 5*23 7c 28*20 a 17*20 7c 5*23 7c 28*20 a
  //   17*20 7c 5*23 7c 28*20 a 52*20 a 52*20 a 52*20 a 52*20 a 52*20 a 52*20 a 52*20 a 52*20 a 52*20 a
  //   52*20 a 52*20
  //   RFL
  //   contents of rom_9 (hex, n*v repeats v):
  //   0 50*20 5f 2f a 48*20 5f 2f 23 23 a 46*20 5f 2f 4*23 a 44*20 5f 2f 6*23 a 43*20 7c 8*23 a 43*20 7c
  //   8*23 a 43*20 7c 8*23 a 43*20 7c 8*23 a 43*20 7c 8*23 a 43*20 7c 8*23 a 43*20 7c 8*23 a 43*20 7c 8*23
  //   a 43*20 7c 8*23 a 43*20 7c 8*23 a 43*20 7c 8*23 a 43*20 7c 8*23 a 43*20 7c 8*23 a 43*20 7c 8*23 a
  //   43*20 7c 8*23 a 43*20 7c 8*23 a 43*20 7c 8*23 a 43*20 7c 8*23 a 43*20 7c 8*23 a 45*20 5c 6*23 a
  //   47*20 5c 4*23 a 49*20 5c 23 23 a 51*20 5c
  //   RFFL
  //   contents of rom_10 (hex, n*v repeats v):
  //   0 51*20 a 52*20 a 52*20 a 52*20 a 41*20 5f 2f 7c 8*20 a 39*20 5f 2f 23 23 7c 8*20 a 37*20 5f 2f 4*23
  //   7c 8*20 a 35*20 5f 2f 6*23 7c 8*20 a 34*20 7c 8*23 7c 8*20 a 34*20 7c 8*23 7c 8*20 a 34*20 7c 8*23
  //   7c 8*20 a 34*20 7c 8*23 7c 8*20 a 34*20 7c 8*23 7c 8*20 a 34*20 7c 8*23 7c 8*20 a 34*20 7c 8*23 7c
  //   8*20 a 34*20 7c 8*23 7c 8*20 a 34*20 7c 8*23 7c 8*20 a 34*20 7c 8*23 7c 8*20 a 34*20 7c 8*23 7c 8*20
  //   a 36*20 5c 6*23 7c 8*20 a 38*20 5c 4*23 7c 8*20 a 40*20 5c 23 23 7c 8*20 a 42*20 5c 7c 8*20 a 52*20
  //   a 52*20 a 52*20 a 52*20
  //   RFFFL
  //   contents of rom_11 (hex, n*v repeats v):
  //   0 51*20 a 52*20 a 52*20 a 52*20 a 52*20 a 52*20 a 52*20 a 35*20 17*5f a 34*20 7c 17*23 a 34*20 7c
  //   17*23 a 34*20 7c 17*23 a 34*20 7c 17*23 a 34*20 7c 17*23 a 34*20 7c 17*23 a 34*20 7c 17*23 a 34*20
  //   7c 17*23 a 34*20 7c 17*23 a 34*20 7c 17*23 a 34*20 7c 17*23 a 52*20 a 52*20 a 52*20 a 52*20 a 52*20
  //   a 52*20 a 52*20 a 52*20
  //   RFFFFL
  //   contents of rom_12 (hex, n*v repeats v):
  //   0 51*20 a 52*20 a 52*20 a 52*20 a 52*20 a 52*20 a 52*20 a 52*20 a 52*20 a 52*20 a 29*20 5*5f 18*20 a
  //   28*20 7c 5*23 7c 17*20 a 28*20 7c 5*23 7c 17*20 a 28*20 7c 5*23 7c 17*20 a 28*20 7c 5*23 7c 17*20 a
  //   28*20 7c 5*23 7c 17*20 a 52*20 a 52*20 a 52*20 a 52*20 a 52*20 a 52*20 a 52*20 a 52*20 a 52*20 a
  //   52*20 a 52*20
  //   FRFL
  //   contents of rom_13 (hex, n*v repeats v):
  //   0 51*20 a 52*20 a 52*20 a 52*20 a 41*20 5f 2f 7c 8*20 a 39*20 5f 2f 23 23 7c 8*20 a 37*20 5f 2f 4*23
  //   7c 8*20 a 35*20 5f 2f 6*23 7c 8*20 a 34*20 7c 8*23 7c 8*20 a 34*20 7c 8*23 7c 8*20 a 34*20 7c 8*23
  //   7c 8*20 a 34*20 7c 8*23 7c 8*20 a 34*20 7c 8*23 7c 8*20 a 34*20 7c 8*23 7c 8*20 a 34*20 7c 8*23 7c
  //   8*20 a 34*20 7c 8*23 7c 8*20 a 34*20 7c 8*23 7c 8*20 a 34*20 7c 8*23 7c 8*20 a 34*20 7c 8*23 7c 8*20
  //   a 36*20 5c 6*23 7c 8*20 a 38*20 5c 4*23 7c 8*20 a 40*20 5c 23 23 7c 8*20 a 42*20 5c 7c 8*20 a 52*20
  //   a 52*20 a 52*20 a 52*20
  //   FLFL
  //   contents of rom_14 (hex, n*v repeats v):
  //   0 51*20 a 52*20 a 52*20 a 52*20 a 8*20 7c 5c 5f 41*20 a 8*20 7c 23 23 5c 5f 39*20 a 8*20 7c 4*23 5c
  //   5f 37*20 a 8*20 7c 6*23 5c 5f 35*20 a 8*20 7c 8*23 7c 34*20 a 8*20 7c 8*23 7c 34*20 a 8*20 7c 8*23
  //   7c 34*20 a 8*20 7c 8*23 7c 34*20 a 8*20 7c 8*23 7c 34*20 a 8*20 7c 8*23 7c 34*20 a 8*20 7c 8*23 7c
  //   34*20 a 8*20 7c 8*23 7c 34*20 a 8*20 7c 8*23 7c 34*20 a 8*20 7c 8*23 7c 34*20 a 8*20 7c 8*23 7c
  //   34*20 a 8*20 7c 6*23 2f 36*20 a 8*20 7c 4*23 2f 38*20 a 8*20 7c 23 23 2f 40*20 a 8*20 7c 2f 42*20 a
  //   52*20 a 52*20 a 52*20 a 52*20
  //   FFRFL
  //   contents of rom_15 (hex, n*v repeats v):
  //   0 51*20 a 52*20 a 52*20 a 52*20 a 52*20 a 52*20 a 52*20 a 52*20 a 32*20 5f 2f 7c 17*20 a 30*20 5f 2f
  //   23 23 7c 17*20 a 29*20 2f 4*23 7c 17*20 a 28*20 7c 5*23 7c 17*20 a 28*20 7c 5*23 7c 17*20 a 28*20 7c
  //   5*23 7c 17*20 a 28*20 7c 5*23 7c 17*20 a 28*20 7c 5*23 7c 17*20 a 29*20 5c 4*23 7c 17*20 a 31*20 5c
  //   23 23 7c 17*20 a 33*20 5c 7c 17*20 a 52*20 a 52*20 a 52*20 a 52*20 a 52*20 a 52*20 a 52*20 a 52*20
  //   FFLFL
  //   contents of rom_16 (hex, n*v repeats v):
  //   0 51*20 a 52*20 a 52*20 a 52*20 a 52*20 a 52*20 a 52*20 a 52*20 a 17*20 7c 5c 5f 32*20 a 17*20 7c 23
  //   23 5c 5f 30*20 a 17*20 7c 4*23 5c 29*20 a 17*20 7c 5*23 7c 28*20 a 17*20 7c 5*23 7c 28*20 a 17*20 7c
  //   5*23 7c 28*20 a 17*20 7c 5*23 7c 28*20 a 17*20 7c 5*23 7c 28*20 a 17*20 7c 4*23 2f 29*20 a 17*20 7c
  //   23 23 2f 31*20 a 17*20 7c 2f 33*20 a 52*20 a 52*20 a 52*20 a 52*20 a 52*20 a 52*20 a 52*20 a 52*20
  //   contents of rom_17 (hex, n*v repeats v):
  //   0 76*23 a 23 74*20 23 a 23 74*20 23 a 23 74*20 23 a 23 26*20 5*5f 20 20 5f 40*20 23 a 23 25*20 7c 5f
  //   20 20 20 5f 7c 7c 20 7c 39*20 23 a 23 27*20 7c 20 7c 20 20 7c 20 7c 5f 5f 4*20 5f 5f 5f 30*20 23 a
  //   23 27*20 7c 20 7c 20 20 7c 20 27 5f 20 5c 20 20 2f 20 5f 20 5c 29*20 23 a 23 27*20 7c 20 7c 20 20 7c
  //   20 7c 20 7c 20 7c 7c 20 20 5f 5f 2f 29*20 23 a 23 27*20 5c 5f 2f 20 20 7c 5f 7c 20 7c 5f 7c 20 5c 5f
  //   5f 5f 7c 29*20 23 a 23 20 5f 5f 5f 20 20 5f 5f 5f 8*20 5f 7*20 5f 7*20 5f 40*20 23 a 23 20 7c 20 20
  //   5c 2f 20 20 7c 7*20 7c 20 7c 5*20 28 20 29 5*20 7c 20 7c 39*20 23 a 23 20 7c 20 2e 20 20 2e 20 7c 20
  //   20 5f 5f 5f 20 20 7c 20 7c 20 20 5f 5f 5f 7c 2f 20 5f 5f 5f 20 20 7c 20 7c 5f 5f 20 20 20 5f 20 20
  //   20 5f 20 20 5f 20 5f 5f 20 20 5f 20 5f 5f 20 20 5f 5f 5f 20 5f 5f 6*20 5f 5f 20 23 a 23 20 7c 20 7c
  //   5c 2f 7c 20 7c 20 2f 20 5f 20 5c 20 7c 20 7c 20 2f 20 5f 20 5c 20 2f 20 5f 5f 7c 20 7c 20 27 5f 20
  //   5c 20 7c 20 7c 20 7c 20 7c 7c 20 27 5f 5f 7c 7c 20 27 5f 5f 7c 2f 20 5f 20 5c 5c 20 5c 20 2f 5c 20
  //   2f 20 2f 20 23 a 23 20 7c 20 7c 20 20 7c 20 7c 7c 20 28 5f 29 20 7c 7c 20 7c 7c 20 20 5f 5f 2f 20 5c
  //   5f 5f 20 5c 20 7c 20 7c 5f 29 20 7c 7c 20 7c 5f 7c 20 7c 7c 20 7c 20 20 20 7c 20 7c 20 20 7c 20 28
  //   5f 29 20 7c 5c 20 56 20 20 56 20 2f 20 20 23 a 23 20 5c 5f 7c 20 20 7c 5f 2f 20 5c 5f 5f 5f 2f 20 7c
  //   5f 7c 20 5c 5f 5f 5f 7c 20 7c 5f 5f 5f 2f 20 7c 5f 2e 5f 5f 2f 20 20 5c 5f 5f 2c 5f 7c 7c 5f 7c 20
  //   20 20 7c 5f 7c 20 20 20 5c 5f 5f 5f 2f 20 20 5c 5f 2f 5c 5f 2f 20 20 20 23 a 23 74*20 23 a 23 74*20
  //   23 a 23 74*20 23 a 23 74*20 23 a 23 74*20 23 a 23 74*20 23 a 23 74*20 23 a 23 74*20 23 a 23 74*20 23
  //   a 23 74*20 23 a 23 74*20 23 a 23 74*20 23 a 23 74*20 23 a 23 74*20 23 a 23 74*20 23 a 23 74*20 23 a
  //   23 74*20 23 a 23 39*20 50 52 45 53 53 20 41 4e 59 20 4b 45 59 20 54 4f 20 43 4f 4e 54 49 4e 55 45 2e
  //   2e 2e 7*20 23 a 23 74*20 23 a 76*23 a 52*20
  //   contents of rom_18 (hex, n*v repeats v):
  //   0 76*23 a 23 74*20 23 a 23 74*20 23 a 23 74*20 23 a 23 74*20 23 a 23 74*20 23 a 23 74*20 23 a 23
  //   74*20 23 a 23 74*20 23 a 23 9*20 7c 14*20 7c 13*20 7c 24*20 7c 20 28 20 20 7c 20 20 29 20 20 23 a 23
  //   74*20 23 a 23 74*20 23 a 23 74*20 23 a 23 74*20 23 a 23 74*20 23 a 23 74*20 23 a 23 74*20 23 a 23
  //   74*20 23 a 23 74*20 23 a 23 4*20 65*2d 5*20 23 a 23 74*20 23 a 23 20*20 5e 24*20 2e 28*20 23 a 23
  //   8*20 2e 19*20 2e 10*20 2e 18*20 2e 7*20 2e 7*20 23 a 23 16*20 2e 17*20 2e 17*20 5e 7*20 2e 13*20 23
  //   a 23 23*20 2e 18*20 2e 31*20 23 a 23 6*20 2e 6*20 5e 16*20 5e 23*20 2e 19*20 23 a 23 23*20 2e 11*20
  //   2e 5*20 2e 20*20 5e 11*20 23 a 23 74*20 23 a 76*23 a 23 74*20 23 a 76*23 a 23 9*20 23 9*20 23 9*20
  //   23 9*20 23 9*20 23 20 48 50 20 7c 10*20 7c 28 20 20 2f 31 30 29 20 23 a 23 9*20 23 9*20 23 9*20 23
  //   9*20 23 9*20 23 20 53 54 20 7c 10*20 7c 28 20 20 2f 31 30 29 20 23 a 23 9*20 23 9*20 23 9*20 23 9*20
  //   23 9*20 23 20 48 47 20 7c 10*20 7c 28 20 20 2f 31 30 29 20 23 a 23 9*20 23 9*20 23 9*20 23 9*20 23
  //   9*20 23 24*20 23 a 76*23 a 52*20
  //   START SCREEN
  //   ATACK BOARD
endmodule

// Maps
module maps (
  input  [7:0] Map_No,
  input  [11:0] Addr_on_map,
  output [11:0] Width,
  output [11:0] Height,
  output [7:0] Xpp,
  output [7:0] Ypp,
  output [7:0] DATA,
  output [11:0] LEN
);

  wire [7:0] mgeD0, mgeD1, undriven_3, undriven_4;
  wire [11:0] undriven, undriven_2;

  ROM #(.addrWidth(12)) rom_1 (.addr(Addr_on_map), .data(mgeD1));  // open: sel
  ROM #(.addrWidth(12)) rom_2 (.addr(Addr_on_map), .data(mgeD0));  // open: sel
  Multiplexer #(.select(5), .width(8), .enable("false")) multiplexer_1 (
    .in0(mgeD0), .in1(mgeD1), .out(DATA), .sel(Map_No[4:0]));  // open: in2, in3, in4, in5, in6, in7, in8, in9, in10, in11, in12, in13, in14, in15, in16, in17, in18, in19, in20, in21, in22, in23, in24, in25, in26, in27, in28, in29, in30, in31
  Multiplexer #(.select(5), .width(12), .enable("false")) multiplexer_2 (
    .in0(12'h99), .out(LEN), .sel(Map_No[4:0]));  // open: in1, in2, in3, in4, in5, in6, in7, in8, in9, in10, in11, in12, in13, in14, in15, in16, in17, in18, in19, in20, in21, in22, in23, in24, in25, in26, in27, in28, in29, in30, in31
  Multiplexer #(.select(5), .width(12), .enable("false")) multiplexer_3 (
    .in0(12'hc), .in1(12'h9), .in30(undriven), .in31(undriven), .out(Width), .sel(Map_No[4:0]));  // open: in2, in3, in4, in5, in6, in7, in8, in9, in10, in11, in12, in13, in14, in15, in16, in17, in18, in19, in20, in21, in22, in23, in24, in25, in26, in27, in28, in29
  Multiplexer #(.select(5), .width(12), .enable("false")) multiplexer_4 (
    .in0(12'hc), .in1(12'h7), .in30(undriven_2), .in31(undriven_2), .out(Height), .sel(Map_No[4:0]));  // open: in2, in3, in4, in5, in6, in7, in8, in9, in10, in11, in12, in13, in14, in15, in16, in17, in18, in19, in20, in21, in22, in23, in24, in25, in26, in27, in28, in29
  Multiplexer #(.select(5), .width(8), .enable("false")) multiplexer_5 (
    .in0(8'h5), .in1(8'h3), .in30(undriven_3), .in31(undriven_3), .out(Xpp), .sel(Map_No[4:0]));  // open: in2, in3, in4, in5, in6, in7, in8, in9, in10, in11, in12, in13, in14, in15, in16, in17, in18, in19, in20, in21, in22, in23, in24, in25, in26, in27, in28, in29
  Multiplexer #(.select(5), .width(8), .enable("false")) multiplexer_6 (
    .in0(8'h5), .in1(8'h2), .in30(undriven_4), .in31(undriven_4), .out(Ypp), .sel(Map_No[4:0]));  // open: in2, in3, in4, in5, in6, in7, in8, in9, in10, in11, in12, in13, in14, in15, in16, in17, in18, in19, in20, in21, in22, in23, in24, in25, in26, in27, in28, in29

  // Other names for the same wires on the sheet: map_char[7:0] = DATA; mgeAddr1[4:0] = Map_No[4:0];
  //   mdeMuxl1[11:0] = LEN; mgeEl[11:0] = Addr_on_map

  // Notes on the sheet:
  //   TEST MAP
  //   contents of rom_1 (hex, n*v repeats v):
  //   0 4 3 2 36*23 20 66 6a 61 20 6*23 20 23 23 20 32 6*23 20 20 23 23 20 36*23
  //   contents of rom_2 (hex, n*v repeats v):
  //   40*23 20 23 20 20 20 7*23 20 23 20 23 20 6*23 20 20 50 20 23 20 6*23 20 23 4*20 6*23 20 23 23 20
  //   8*23 20 20 23 20 20 20 39*23
endmodule

module printing_map (
  input  [7:0] No_of_map,
  input  [7:0] Xpp,
  input  [7:0] Ypp,
  input  Clock,
  input  [7:0] Num_of_elem,
  input  [11:0] Mem_N,
  input  Main_Res,
  output [7:0] Char_on_screen,
  output Cond_of_change
);

  wire and_1_out, and_3_out, comparator_1_eq, comparator_2_eq, comparator_3_eq, comparator_4_lt,
       comparator_5_gt, comparator_5_lt, comparator_6_eq, not_1_out, not_2_out, not_3_out, or_1_out,
       or_2_out, partition_on_sections_1_condition_of_writing;
  wire [4:0] adder_13_out, register_2_q;
  wire [7:0] maps_1_data, maps_2_data, maps_3_data, maps_4_data, maps_5_data, maps_6_data, maps_7_data;
  wire [11:0] adder_1_out, adder_2_out, adder_3_out, adder_4_out, adder_5_out, divider_1_rem, Height,
       multiplier_1_out, num1, num2, num3, num4, num5, num6, num7, register_1_q, Width;

  Register #(.width(12)) register_1 (.D(adder_2_out), .Q(register_1_q), .clk(and_1_out), .clr(or_1_out));  // open: en
  or or_1 (or_1_out, comparator_1_eq, Main_Res);
  Adder #(.width(12)) adder_1 (.a(12'hffd), .b(register_1_q), .out(adder_1_out));  // open: cin, cout
  Comparator #(.width(12), .mode("unsigned")) comparator_1 (
    .a(12'h8), .b(register_1_q), .eq(comparator_1_eq));  // open: gt, lt
  Adder #(.width(12)) adder_2 (.a(register_1_q), .b(12'h1), .out(adder_2_out));  // open: cin, cout
  Comparator #(.mode("unsigned")) comparator_2 (.a(Num_of_elem), .b({8{1'b0}}), .eq(comparator_2_eq));  // open: gt, lt
  Adder #(.width(12)) adder_3 (.a({4'b0000, Ypp}), .b(adder_1_out), .out(adder_3_out));  // open: cin, cout
  Divider #(.width(12)) divider_1 (.a(Mem_N), .b(12'he7), .rem(divider_1_rem));  // open: out, upper
  Comparator #(.width(12), .mode("unsigned")) comparator_3 (
    .a(divider_1_rem), .b(12'h83), .eq(comparator_3_eq));  // open: gt, lt
  Comparator #(.width(12), .mode("unsigned")) comparator_4 (
    .a(Mem_N), .b(12'h6b2), .lt(comparator_4_lt));  // open: gt, eq
  Comparator #(.width(12), .mode("unsigned")) comparator_5 (
    .a(Mem_N), .b(12'h83), .gt(comparator_5_gt), .lt(comparator_5_lt));  // open: eq
  Multiplier #(.width(12)) multiplier_1 (.a(Width), .b(adder_3_out), .out(multiplier_1_out));  // open: cin, cout
  // Probe on multiplier_1_out
  and and_1 (and_1_out, comparator_2_eq, comparator_3_eq, comparator_4_lt, comparator_5_gt);
  not not_1 (not_1_out, comparator_5_lt);
  Adder #(.width(12)) adder_4 (.a({4'b0000, Xpp}), .b(12'hffd), .out(adder_4_out));  // open: cin, cout
  Adder #(.width(12)) adder_5 (.a(adder_4_out), .b(multiplier_1_out), .out(adder_5_out));  // open: cin, cout
  partition_on_sections partition_on_sections_1 (
    .Reminder(divider_1_rem), .Condition_of_writing(partition_on_sections_1_condition_of_writing));
  Adder #(.width(12)) adder_6 (.a(adder_5_out), .b({12{1'b0}}), .out(num1));  // open: cin, cout
  Adder #(.width(12)) adder_7 (.a(adder_5_out), .b(12'h1), .out(num2));  // open: cin, cout
  Adder #(.width(12)) adder_8 (.a(adder_5_out), .b(12'h2), .out(num3));  // open: cin, cout
  Adder #(.width(12)) adder_9 (.a(adder_5_out), .b(12'h3), .out(num4));  // open: cin, cout
  Adder #(.width(12)) adder_10 (.a(adder_5_out), .b(12'h4), .out(num5));  // open: cin, cout
  Adder #(.width(12)) adder_11 (.a(adder_5_out), .b(12'h5), .out(num6));  // open: cin, cout
  Adder #(.width(12)) adder_12 (.a(adder_5_out), .b(12'h6), .out(num7));  // open: cin, cout
  and and_2 (Cond_of_change, partition_on_sections_1_condition_of_writing, not_1_out, comparator_2_eq, comparator_4_lt);
  // Probe on num1
  // Probe on num2
  // Probe on num3
  // Probe on num4
  // Probe on num5
  // Probe on num6
  // Probe on num7
  maps maps_1 (
    .Map_No(No_of_map), .Addr_on_map(num1), .DATA(maps_1_data), .Width(Width), .Height(Height));  // open: LEN, Xpp, Ypp
  maps maps_2 (.Map_No(No_of_map), .Addr_on_map(num2), .DATA(maps_2_data));  // open: LEN, Xpp, Ypp, Width, Height
  maps maps_3 (.Map_No(No_of_map), .Addr_on_map(num3), .DATA(maps_3_data));  // open: LEN, Xpp, Ypp, Width, Height
  maps maps_4 (.Map_No(No_of_map), .Addr_on_map(num4), .DATA(maps_4_data));  // open: LEN, Xpp, Ypp, Width, Height
  maps maps_5 (.Map_No(No_of_map), .Addr_on_map(num5), .DATA(maps_5_data));  // open: LEN, Xpp, Ypp, Width, Height
  maps maps_6 (.Map_No(No_of_map), .Addr_on_map(num6), .DATA(maps_6_data));  // open: LEN, Xpp, Ypp, Width, Height
  maps maps_7 (.Map_No(No_of_map), .Addr_on_map(num7), .DATA(maps_7_data));  // open: LEN, Xpp, Ypp, Width, Height
  // Probe on maps_1_data
  // Probe on maps_2_data
  // Probe on maps_3_data
  // Probe on maps_4_data
  // Probe on maps_5_data
  // Probe on maps_6_data
  // Probe on maps_7_data
  Multiplexer #(.select(5), .width(8)) multiplexer_1 (
    .in0(maps_1_data), .in1(maps_1_data), .in2(maps_1_data), .in3(maps_2_data), .in4(maps_2_data),
    .in5(maps_2_data), .in6(maps_3_data), .in7(maps_3_data), .in8(maps_3_data), .in9(maps_4_data),
    .in10(maps_4_data), .in11(maps_4_data), .in12(maps_5_data), .in13(maps_5_data), .in14(maps_5_data),
    .in15(maps_6_data), .in16(maps_6_data), .in17(maps_6_data), .in18(maps_7_data), .in19(maps_7_data),
    .in20(maps_7_data), .out(Char_on_screen), .sel(register_2_q));  // open: in21, in22, in23, in24, in25, in26, in27, in28, in29, in30, in31, en
  or or_2 (or_2_out, Main_Res, and_3_out);
  not not_2 (not_2_out, not_3_out);
  not not_3 (not_3_out, or_2_out);
  Register #(.width(5)) register_2 (
    .D(adder_13_out), .Q(register_2_q), .clk(not_2_out), .clr(comparator_6_eq));  // open: en
  and and_3 (and_3_out, Cond_of_change, Clock);
  Adder #(.width(5)) adder_13 (.a(register_2_q), .b(5'b00001), .out(adder_13_out));  // open: cin, cout
  Comparator #(.width(5), .mode("unsigned")) comparator_6 (
    .a(5'b10111), .b(register_2_q), .eq(comparator_6_eq));  // open: gt, lt

  // Other names for the same wires on the sheet: No[7:0] = No_of_map; Res = Main_Res
endmodule

module x_y__to_memory_elem_number (
  input  [11:0] H,
  input  [7:0] Y,
  input  [7:0] X,
  input  [11:0] START,
  output [11:0] ELEM
);

  wire [11:0] adder_1_out, bit_extender_1_out, bit_extender_2_out, multiplier_1_out;

  assign bit_extender_1_out = {{4{1'b0}}, Y};  // Bit_Extender bit_extender_1
  Multiplier #(.width(12)) multiplier_1 (.a(H), .b(bit_extender_1_out), .out(multiplier_1_out));  // open: cin, cout
  assign bit_extender_2_out = {{4{1'b0}}, X};  // Bit_Extender bit_extender_2
  Adder #(.width(12)) adder_1 (.a(multiplier_1_out), .b(bit_extender_2_out), .out(adder_1_out));  // open: cin, cout
  Adder #(.width(12)) adder_2 (.a(adder_1_out), .b(START), .out(ELEM));  // open: cin, cout
endmodule

module enemies (
  input  [1:0] ADDR,
  input  [7:0] ELEMIm,
  input  [7:0] ELEMNm,
  output [7:0] Img,
  output [7:0] Txt,
  output [7:0] HP,
  output [7:0] DMG
);

  wire [7:0] EnImEl1, EnImEl1txt, EnImEl2, EnImEl2txt, EnImEl3, EnImEl3txt, EnImEl4, EnImEl4txt;

  ROM rom_1 (.addr(ELEMIm), .data(EnImEl1));  // open: sel
  ROM rom_2 (.addr(ELEMIm), .data(EnImEl2));  // open: sel
  ROM rom_3 (.addr(ELEMIm), .data(EnImEl3));  // open: sel
  ROM rom_4 (.addr(ELEMIm), .data(EnImEl4));  // open: sel
  Multiplexer #(.select(2), .width(8), .enable("false")) multiplexer_1 (
    .in0(EnImEl1), .in1(EnImEl2), .in2(EnImEl3), .in3(EnImEl4), .out(Img), .sel(ADDR));
  Multiplexer #(.select(2), .width(8), .enable("false")) multiplexer_2 (
    .in0(EnImEl1txt), .in1(EnImEl2txt), .in2(EnImEl3txt), .in3(EnImEl4txt), .out(Txt), .sel(ADDR));
  Multiplexer #(.select(2), .width(8), .disabled(0), .enable("false")) multiplexer_3 (
    .in0(8'h24), .in1(8'h12), .in2(8'h62), .in3(8'h36), .out(HP), .sel(ADDR));
  Multiplexer #(.select(2), .width(8), .disabled(0), .enable("false")) multiplexer_4 (
    .in0(8'h5), .in1(8'h3), .in2(8'h24), .in3(8'h12), .out(DMG), .sel(ADDR));
  ROM rom_5 (.addr(ELEMIm), .data(EnImEl1txt));  // open: sel
  ROM rom_6 (.addr(ELEMIm), .data(EnImEl2txt));  // open: sel
  ROM rom_7 (.addr(ELEMIm), .data(EnImEl3txt));  // open: sel
  ROM rom_8 (.addr(ELEMIm), .data(EnImEl4txt));  // open: sel

  // Other names for the same wires on the sheet: enaddr1[1:0] = ADDR; EnImEl[7:0] = ELEMIm; EnImEltxt[7:0] = ELEMNm

  // Notes on the sheet:
  //   rat
  //   mouse
  //   ferret
  //   snake
  //   contents of rom_1 (hex, n*v repeats v):
  //   15*20 35 64 6d 67 2e 9*20 2f 5c 5f 2f 5c 16*20 28 20 6f 20 6f 20 29 15*20 2f 20 20 56 20 20 5c 15*20
  //   2f 20 3e 20 20 3c 20 20 5c 12*20 28 20 2f 5*20 5c 20 29 20 20 20 7c 8*20 5c 5f 20 4*2d 20 5f 2f 5f
  //   5f 5f 2f 24*20
  //   contents of rom_2 (hex, n*v repeats v):
  //   13*20 33 64 6d 67 2e 13*20 2f 5e 5c 5e 5c 5f 10*20 2f 4*20 7c 5*20 6f 5c 5f 7*20 7c 4*20 2f 7*20 5f
  //   2f 7*20 5c 20 20 20 2f 6*20 5f 5f 3e 9*20 5c 5f 5f 7c 20 20 20 5f 5f 5f 29 14*20 5c 5f 5f 5f 7c 5c
  //   5f 5f 30*20
  //   contents of rom_3 (hex, n*v repeats v):
  //   14*20 32 30 64 6d 67 2e 8*20 2f 29 5*5f 28 5c 12*20 28 2f 20 6f 20 20 20 6f 20 5c 29 11*20 7c 4*20
  //   4f 4*20 7c 12*20 5c 20 20 2d 5e 2d 20 20 2f 13*20 2f 7*20 5c 12*20 7c 9*20 7c 28*20
  //   contents of rom_4 (hex, n*v repeats v):
  //   14*20 31 30 64 6d 67 2e 4*20 2e 2d 2e 17*20 3e 2d 30 5f 30 29 29 20 20 7c 20 20 2f 20 29 11*20 2f 2f
  //   20 20 20 7c 2e 2f 5f 5f 29 10*20 28 28 5f 2e 2d 2d 27 20 5f 20 20 27 2e 10*20 60 2d 5f 5f 2d 2d 27
  //   20 27 2d 2e 20 29 16*20 5f 5f 2d 2d 27 28*20
  //   rat
  //   mouse
  //   ferret
  //   snake
  //   8x22 = 176
  //   20 chars name len
  //   contents of rom_5 (hex, n*v repeats v):
  //   6*20 53 43 41 52 59 20 52 41 54 5*20
  //   contents of rom_6 (hex, n*v repeats v):
  //   5*20 45 56 49 4c 20 4d 4f 55 53 45 5*20
  //   contents of rom_7 (hex, n*v repeats v):
  //   4*20 43 55 54 45 20 46 45 52 52 45 54 5*20
  //   contents of rom_8 (hex, n*v repeats v):
  //   4*20 4c 49 54 54 4c 45 20 53 4e 41 4b 45 4*20
endmodule

module quick (
  input  IN,
  output OUT
);

  wire not_1_out, not_2_out;

  not not_1 (not_1_out, IN);
  Register #(.width(1)) register_1 (.D(IN), .Q(OUT), .clk(IN), .clr(not_2_out));  // open: en
  not not_2 (not_2_out, not_1_out);
endmodule

module food (
  input  [7:0] FOOD,
  output [7:0] GIVEHP
);

  wire [1:0] bit_extender_1_out;
  wire [7:0] subtractor_1_out;

  Subtractor subtractor_1 (.a(FOOD), .b(8'h61), .out(subtractor_1_out));  // open: bin, bout
  Multiplexer #(.select(2), .width(8), .enable("false")) multiplexer_1 (
    .in0(8'h5), .in1(8'h3), .in2(8'h7), .in3(8'ha), .out(GIVEHP), .sel(bit_extender_1_out));
  Bit_Extender #(.out_width(2)) bit_extender_1 (.in(subtractor_1_out), .out(bit_extender_1_out));

  // Notes on the sheet:
  //   const/2
endmodule

module Lquick (
  input  IN,
  input  CLC,
  output OUT
);

  wire and_1_out, comparator_1_eq, quick_1_out;
  wire [2:0] adder_1_out, register_1_q;

  and and_1 (and_1_out, CLC, ~comparator_1_eq);  // AND_Gate
  quick quick_1 (.IN(IN), .OUT(quick_1_out));
  Adder #(.width(3)) adder_1 (.a(3'b001), .b(register_1_q), .out(adder_1_out));  // open: cin, cout
  Comparator #(.width(3), .mode("unsigned")) comparator_1 (
    .a(3'b111), .b(register_1_q), .gt(OUT), .eq(comparator_1_eq));  // open: lt
  Register #(.width(3)) register_1 (.D(adder_1_out), .Q(register_1_q), .clk(and_1_out), .clr(quick_1_out));  // open: en
endmodule

module weapon (
  input  [7:0] WEAPON,
  output [7:0] DMG
);

  wire [2:0] bit_extender_1_out;
  wire [7:0] subtractor_1_out;

  Subtractor subtractor_1 (.a(WEAPON), .b(8'h66), .out(subtractor_1_out));  // open: bin, bout
  Multiplexer #(.select(3), .width(8), .enable("false")) multiplexer_1 (
    .in0(8'h5), .in1(8'h14), .in2(8'hf), .in3(8'ha), .in4({8{1'b1}}), .out(DMG), .sel(bit_extender_1_out));  // open: in5, in6, in7
  Bit_Extender #(.out_width(3)) bit_extender_1 (.in(subtractor_1_out), .out(bit_extender_1_out));
endmodule

module partition_on_sections (
  input  [11:0] Reminder,
  output Condition_of_writing
);

  wire and_1_out, and_2_out, and_3_out, and_4_out, comparator_1_lt, comparator_2_lt, comparator_3_lt,
       comparator_4_lt, comparator_5_lt, comparator_6_lt, comparator_7_lt, comparator_8_lt, not_1_out,
       not_2_out, not_3_out, not_4_out, not_5_out, not_6_out, not_7_out, not_8_out, or_1_out;

  Comparator #(.width(12), .mode("unsigned")) comparator_1 (
    .a(Reminder), .b(12'h82), .lt(comparator_1_lt));  // open: gt, eq
  Comparator #(.width(12), .mode("unsigned")) comparator_2 (
    .a(Reminder), .b(12'h97), .lt(comparator_2_lt));  // open: gt, eq
  Comparator #(.width(12), .mode("unsigned")) comparator_3 (
    .a(Reminder), .b(12'hcf), .lt(comparator_3_lt));  // open: gt, eq
  Comparator #(.width(12), .mode("unsigned")) comparator_4 (
    .a(Reminder), .b(12'he6), .lt(comparator_4_lt));  // open: gt, eq
  Comparator #(.width(12), .mode("unsigned")) comparator_5 (
    .a(Reminder), .b({12{1'b0}}), .lt(comparator_5_lt));  // open: gt, eq
  Comparator #(.width(12), .mode("unsigned")) comparator_6 (
    .a(Reminder), .b(12'h7), .lt(comparator_6_lt));  // open: gt, eq
  Comparator #(.width(12), .mode("unsigned")) comparator_7 (
    .a(Reminder), .b(12'h35), .lt(comparator_7_lt));  // open: gt, eq
  Comparator #(.width(12), .mode("unsigned")) comparator_8 (
    .a(Reminder), .b(12'h74), .lt(comparator_8_lt));  // open: gt, eq
  not not_1 (not_1_out, comparator_1_lt);
  not not_2 (not_2_out, comparator_2_lt);
  not not_3 (not_3_out, comparator_3_lt);
  not not_4 (not_4_out, comparator_4_lt);
  not not_5 (not_5_out, comparator_5_lt);
  not not_6 (not_6_out, comparator_6_lt);
  not not_7 (not_7_out, comparator_7_lt);
  not not_8 (not_8_out, comparator_8_lt);
  and and_1 (and_1_out, not_1_out, not_2_out);
  and and_2 (and_2_out, not_3_out, not_4_out);
  and and_3 (and_3_out, not_5_out, not_6_out);
  and and_4 (and_4_out, not_7_out, not_8_out);
  or or_1 (or_1_out, and_2_out, and_3_out);
  or or_2 (Condition_of_writing, and_1_out, or_1_out, and_4_out);
endmodule
